// Digital circuit SACCO.dig.dig as structural Verilog
module SACCO_dig (
  input  R4,
  input  R3,
  input  R2,
  input  R1,
  output Y1,
  output Y0,
  output V
);

  wire and_1_out, not_1_out;

  or or_1 (Y1, R4, R3);
  not not_1 (not_1_out, R3);
  and and_1 (and_1_out, not_1_out, R2);
  or or_2 (V, R4, R3, R2, R1);
  or or_3 (Y0, R4, and_1_out);
endmodule
